# Fritzing sketch readsensor (saved by Fritzing 0.9.3b)
circuit board: 8.46667cm x 5.64444cm
breadboards: 1

parts:
  U1 = NodeMCU V3.0
  Squix1 = OLED 0.96" 128x64 I2C SSD1306
  R1 = Resistor [tolerance=±5% resistance=4.7k package=THT]
  R2 = Resistor [tolerance=±5% resistance=4.7k package=THT]
  DHT1 = DHT11 Humitidy and Temperature Sensor
  R3 = Resistor [tolerance=±5% resistance=10k package=THT]
  Part1 = Barometric Pressure Sensor - BMP180 Breakout (GY-68)

nets:
  N1: U1.D1, Squix1.SCL, R2.Pin_1, Part1.SCL
  N2: U1.D2, Squix1.SCA, R1.Pin_1, Part1.SDA
  N3: U1.D4, DHT1.DATA, R3.Pin_1
  3V3: U1.3V3, DHT1.VDD, R3.Pin_0, Part1.VCC
  GND: U1.GND#6, U1.GND#13, U1.GND#16, U1.GND#33, Squix1.GND, DHT1.GND, Part1.GND
  N4: U1.VU, Squix1.VCC, R1.Pin_0, R2.Pin_0

custom parts:
  NodeMCU V3.0: ESP8266 based NodeMCU
  DHT11 Humitidy and Temperature Sensor: DHT11 Humidity and Temperature Sensor
